// Logisim project PB1204microcode.circ as structural Verilog: 1 circuit, main circuit main
module main (
  input  [3:0] RegisterNumber,
  input  [3:0] FunctionNumber,
  input  [3:0] DATA,
  input  BitmaskEnable,
  input  in_5,
  input  in_6
);

  wire and_1_out, and_3_out, and_4_out, and_5_out, and_6_out, and_7_out, and_8_out, and_9_out, and_10_out,
       and_11_out, and_12_out, and_13_out, and_14_out, and_15_out, and_16_out, and_17_out, and_18_out,
       and_19_out, and_20_out, and_23_out, and_24_out, and_25_out, and_26_out, ARegisterEnable, Bitdepth,
       BitmaskEnable_t, BitmaskRegisterEnable, BorrowFlag, BorrowResult, BRegisterEnable,
       Buffer0RegisterEnable, Buffer1RegisterEnable, Buffer2RegisterEnable, CarryFlag, CarryResult,
       CheckIfFlag, CLK, CycleReset, DecrementRegister, demultiplexer_2_out8, demultiplexer_2_out9,
       demultiplexer_2_out10, demultiplexer_2_out11, demultiplexer_2_out12, demultiplexer_2_out13,
       demultiplexer_2_out14, demultiplexer_2_out15, demultiplexer_3_out5, demultiplexer_3_out9,
       demultiplexer_3_out13, FlagsRegisterEnable, GeneralReset, HardwareReset, IncrementRegister,
       InstructionRegisterEnable, InterruptModeRegisterEnable, not_3_out, not_4_out, not_5_out, not_6_out,
       or_1_out, or_2_out, or_3_out, or_4_out, or_6_out, or_9_out, or_10_out, or_11_out, or_12_out,
       or_13_out, PC0_carry, PC0Enable, PC1_carry, PC1Enable, PC2Enable, ReadFromBuffer, ReadFromDatabus,
       ResetRegister, s_r_ff_2_qn, SkipMicrocode, SP0Enable, SP1Enable, SP2Enable, TestBorrowFlag,
       TestCarryFlag, TestFlagsRegisterEnable, TriggerUpdateOfRegister, WriteToAddressRegister,
       WriteToDatabus, xor_1_out, xor_2_out, xor_3_out;
  wire [3:0] AData, ALUData, and_2_out, BData, BitmaskRegister, Buffer0Register_q, Buffer1Data, Buffer2Data,
       controlled_buffer_5_out, CycleCounter, DATABUS, FlagsRegister, FuncID, InstructionRegister,
       InternalDatabus, InterruptModeRegister, MicrocodeRegister, not_1_out, PC0Data, PC1Data, PC2Data,
       RegID, SP0Data, SP1Data, SP2Data, TestFlagsRegister;
  wire [8:0] rom_1_data;
  wire [11:0] ADDRESSBUS;

  // Probe on CycleCounter
  // Probe on InstructionRegister
  // Probe on Bitdepth
  ROM #(.addrWidth(9), .dataWidth(9)) rom_1 (.addr({Bitdepth, InstructionRegister, CycleCounter}), .data(rom_1_data));
  xor xor_1 (xor_1_out, AData[0], AData[1]);
  xor xor_2 (xor_2_out, AData[2], AData[3]);
  and and_1 (and_1_out, not_1_out[3], not_1_out[2], not_1_out[1], not_1_out[0]);
  assign not_1_out = ~{TestFlagsRegister[3], TestBorrowFlag, TestCarryFlag, TestFlagsRegister[0]};  // NOT_Gate not_1, 4 bits wide
  RAM #(.addrWidth(12), .dataWidth(4), .databus("bidir"), .trigger("high"), .\type ("nonvolatile")) ram_1 (
    .addr(ADDRESSBUS), .we(WriteToDatabus), .oe(ReadFromDatabus), .clk(CLK), .data(DATABUS));
  Register #(.width(4)) u_TestFlagsRegister (
    .D(InternalDatabus), .en(TestFlagsRegisterEnable), .clk(TriggerUpdateOfRegister),
    .Q({TestFlagsRegister[3], TestBorrowFlag, TestCarryFlag, TestFlagsRegister[0]}), .clr(HardwareReset));
  nor nor_1 (FlagsRegister[0], AData[0], AData[1], AData[2], AData[3]);
  xor xor_3 (xor_3_out, xor_1_out, xor_2_out);
  assign and_2_out = {TestFlagsRegister[3], TestBorrowFlag, TestCarryFlag, TestFlagsRegister[0]} & {FlagsRegister[3], BorrowFlag, CarryFlag, FlagsRegister[0]};  // AND_Gate and_2, 4 bits wide
  not not_2 (FlagsRegister[3], xor_3_out);
  assign {BitmaskEnable_t, FuncID, MicrocodeRegister} = in_5 ? {BitmaskEnable, FunctionNumber, RegisterNumber} : 9'bz;  // Controlled_Buffer controlled_buffer_1
  not not_3 (not_3_out, in_5);
  Pull_Resistor pull_resistor_1 (.node({BitmaskEnable_t, FuncID, MicrocodeRegister}));
  assign {BitmaskEnable_t, FuncID, MicrocodeRegister} = not_3_out ? rom_1_data : 9'bz;  // Controlled_Buffer controlled_buffer_2
  or or_1 (or_1_out, and_1_out, and_2_out[0], and_2_out[1], and_2_out[2], and_2_out[3]);
  // Probe on DATABUS
  Clock clock_1 (.out(CLK));
  and and_3 (and_3_out, CheckIfFlag, or_1_out);
  S_R_Flip_Flop s_r_ff_1 (.Q(SkipMicrocode), .reset(ResetRegister), .preset(and_3_out));  // open: S, R, clk, Qn
  Pull_Resistor pull_resistor_2 (.node(DATABUS));
  and and_4 (and_4_out, CLK, FuncID[3]);
  // Probe on MicrocodeRegister
  // Probe on FuncID
  // Probe on BitmaskEnable_t
  or or_2 (or_2_out, ReadFromBuffer, and_4_out);
  and and_5 (and_5_out, ResetRegister, TestBorrowFlag);
  S_R_Flip_Flop #(.trigger("falling")) BorrowRegister (
    .S(BorrowResult), .R(not_4_out), .clk(and_6_out), .Q(BorrowFlag), .reset(or_3_out));  // open: Qn, preset
  not not_4 (not_4_out, BorrowResult);
  and and_6 (and_6_out, CLK, FuncID[3]);
  or or_3 (or_3_out, and_5_out, HardwareReset);
  assign RegID = not_5_out ? MicrocodeRegister : 4'bz;  // Controlled_Buffer controlled_buffer_3
  not not_5 (not_5_out, BitmaskEnable_t);
  assign RegID = BitmaskEnable_t ? BitmaskRegister : 4'bz;  // Controlled_Buffer controlled_buffer_4
  assign controlled_buffer_5_out = or_2_out ? ALUData : 4'bz;  // Controlled_Buffer controlled_buffer_5
  or or_4 (or_4_out, or_2_out, ReadFromDatabus);
  assign controlled_buffer_5_out = ReadFromDatabus ? DATABUS : 4'bz;  // Controlled_Buffer controlled_buffer_6
  and and_7 (and_7_out, WriteToDatabus, ARegisterEnable);
  and and_8 (and_8_out, WriteToDatabus, PC0Enable);
  assign DATABUS = and_7_out ? AData : 4'bz;  // Controlled_Buffer controlled_buffer_7
  and and_9 (and_9_out, WriteToDatabus, PC1Enable);
  and and_10 (and_10_out, WriteToDatabus, PC2Enable);
  assign DATABUS = and_8_out ? PC0Data : 4'bz;  // Controlled_Buffer controlled_buffer_8
  assign DATABUS = and_9_out ? PC1Data : 4'bz;  // Controlled_Buffer controlled_buffer_9
  assign DATABUS = and_10_out ? PC2Data : 4'bz;  // Controlled_Buffer controlled_buffer_10
  Register #(.width(4)) Buffer0Register (
    .D(controlled_buffer_5_out), .en(Buffer0RegisterEnable), .clk(or_4_out), .Q(Buffer0Register_q),
    .clr(HardwareReset));
  Register #(.width(4)) Buffer1Register (
    .D(controlled_buffer_5_out), .en(Buffer1RegisterEnable), .clk(or_4_out), .Q(Buffer1Data),
    .clr(HardwareReset));
  Register #(.width(4)) Buffer2Register (
    .D(controlled_buffer_5_out), .en(Buffer2RegisterEnable), .clk(or_4_out), .Q(Buffer2Data),
    .clr(HardwareReset));
  and and_11 (and_11_out, WriteToDatabus, BRegisterEnable);
  and and_12 (and_12_out, WriteToDatabus, SP0Enable);
  and and_13 (and_13_out, WriteToDatabus, SP1Enable);
  assign DATABUS = and_11_out ? BData : 4'bz;  // Controlled_Buffer controlled_buffer_11
  assign DATABUS = and_12_out ? SP0Data : 4'bz;  // Controlled_Buffer controlled_buffer_12
  assign DATABUS = and_13_out ? SP1Data : 4'bz;  // Controlled_Buffer controlled_buffer_13
  or or_5 (TriggerUpdateOfRegister, ReadFromBuffer, ReadFromDatabus);
  not not_6 (not_6_out, CarryResult);
  and and_14 (and_14_out, ResetRegister, TestCarryFlag);
  or or_6 (or_6_out, and_14_out, HardwareReset);
  and and_15 (and_15_out, WriteToDatabus, SP2Enable);
  assign DATABUS = and_15_out ? SP2Data : 4'bz;  // Controlled_Buffer controlled_buffer_14
  Register #(.trigger("high"), .width(4)) u_InstructionRegister (
    .D(InternalDatabus), .en(InstructionRegisterEnable), .clk(and_16_out), .Q(InstructionRegister),
    .clr(GeneralReset));
  and and_16 (and_16_out, InstructionRegisterEnable, TriggerUpdateOfRegister);
  assign InternalDatabus = ReadFromDatabus ? DATABUS : 4'bz;  // Controlled_Buffer controlled_buffer_15
  assign InternalDatabus = ReadFromBuffer ? Buffer0Register_q : 4'bz;  // Controlled_Buffer controlled_buffer_16
  S_R_Flip_Flop #(.trigger("falling")) CarryRegister (
    .S(CarryResult), .R(not_6_out), .clk(and_6_out), .Q(CarryFlag), .reset(or_6_out));  // open: Qn, preset
  Counter #(.max('hf), .trigger("falling"), .width(4)) u_CycleCounter (
    .clr(CycleReset), .clk(CLK), .Q(CycleCounter));  // open: load, up, count, D, carry
  Pull_Resistor pull_resistor_3 (.node(InstructionRegister));
  Demultiplexer #(.select(4)) demultiplexer_1 (
    .out0(InstructionRegisterEnable), .out1(BitmaskRegisterEnable), .out2(FlagsRegisterEnable),
    .out3(TestFlagsRegisterEnable), .out4(InterruptModeRegisterEnable), .out5(Buffer0RegisterEnable),
    .out6(Buffer1RegisterEnable), .out7(Buffer2RegisterEnable), .out8(ARegisterEnable), .out9(PC0Enable),
    .out10(PC1Enable), .out11(PC2Enable), .out12(BRegisterEnable), .out13(SP0Enable), .out14(SP1Enable),
    .out15(SP2Enable), .in(CLK), .sel(RegID));
  Demultiplexer #(.select(4)) demultiplexer_2 (
    .out0(ReadFromDatabus), .out1(WriteToDatabus), .out2(WriteToAddressRegister), .out3(ReadFromBuffer),
    .out4(IncrementRegister), .out5(DecrementRegister), .out6(CheckIfFlag), .out7(ResetRegister),
    .out8(demultiplexer_2_out8), .out9(demultiplexer_2_out9), .out10(demultiplexer_2_out10),
    .out11(demultiplexer_2_out11), .out12(demultiplexer_2_out12), .out13(demultiplexer_2_out13),
    .out14(demultiplexer_2_out14), .out15(demultiplexer_2_out15), .in(CLK), .sel(FuncID));
  Register #(.trigger("high"), .width(4)) u_InterruptModeRegister (
    .D(InternalDatabus), .en(InterruptModeRegisterEnable), .clk(and_17_out), .Q(InterruptModeRegister),
    .clr(HardwareReset));
  and and_17 (and_17_out, InterruptModeRegisterEnable, TriggerUpdateOfRegister);
  Register #(.trigger("high"), .width(4)) u_BitmaskRegister (
    .D(InternalDatabus), .en(BitmaskRegisterEnable), .clk(and_18_out), .Q(BitmaskRegister),
    .clr(HardwareReset));
  and and_18 (and_18_out, BitmaskRegisterEnable, TriggerUpdateOfRegister);
  Demultiplexer #(.select(4)) demultiplexer_3 (
    .out5(demultiplexer_3_out5), .out9(demultiplexer_3_out9), .out13(demultiplexer_3_out13), .in(1'b1),
    .sel(BitmaskRegister));  // open: out0, out1, out2, out3, out4, out6, out7, out8, out10, out11, out12, out14, out15
  and and_19 (and_19_out, ARegisterEnable, TriggerUpdateOfRegister);
  and and_20 (and_20_out, BRegisterEnable, TriggerUpdateOfRegister);
  or or_7 (Bitdepth, demultiplexer_3_out5, demultiplexer_3_out9, demultiplexer_3_out13);
  Register #(.trigger("high"), .width(4)) ARegister (
    .D(InternalDatabus), .en(ARegisterEnable), .clk(and_19_out), .Q(AData), .clr(HardwareReset));
  Register #(.trigger("high"), .width(4)) BRegister (
    .D(InternalDatabus), .en(BRegisterEnable), .clk(and_20_out), .Q(BData), .clr(HardwareReset));
  Pull_Resistor pull_resistor_4 (.node(ALUData));
  pbp1204alu pbp1204alu_1 (
    .NANDenable(demultiplexer_2_out8), .NORenable(demultiplexer_2_out9), .NOTenable(demultiplexer_2_out10),
    .ADDenable(demultiplexer_2_out11), .SLenable(demultiplexer_2_out12), .SRenable(demultiplexer_2_out13),
    .PRIMARYenable(demultiplexer_2_out14), .SECONDARYenable(demultiplexer_2_out15), .PrimaryInput(AData),
    .SecondaryInput(BData), .CarryIn(CarryFlag), .PrimaryOutput(ALUData), .CarryOut(CarryResult),
    .BorrowOut(BorrowResult));
  and and_21 (CycleReset, ResetRegister, FlagsRegisterEnable);
  and and_22 (HardwareReset, ResetRegister, InstructionRegisterEnable);
  Pull_Resistor pull_resistor_5 (.node(Bitdepth));
  or or_8 (GeneralReset, CycleReset, HardwareReset);
  S_R_Flip_Flop s_r_ff_2 (
    .reset(IncrementRegister), .Qn(s_r_ff_2_qn), .preset(DecrementRegister));  // open: S, R, clk, Q
  or or_9 (or_9_out, IncrementRegister, IncrementRegister);
  and and_23 (and_23_out, PC2Enable, SkipMicrocode, TriggerUpdateOfRegister);
  and and_24 (and_24_out, PC1Enable, SkipMicrocode, TriggerUpdateOfRegister);
  and and_25 (and_25_out, PC0Enable, SkipMicrocode, TriggerUpdateOfRegister);
  and and_26 (and_26_out, PC0Enable, or_9_out);
  or or_10 (or_10_out, and_23_out, PC1_carry);
  or or_11 (or_11_out, and_24_out, PC0_carry);
  or or_12 (or_12_out, and_25_out, and_26_out, in_6);
  Counter #(.max('hf), .width(4)) PC2 (
    .clr(HardwareReset), .load(and_23_out), .up(s_r_ff_2_qn), .count(1'b1), .clk(or_10_out),
    .D(InternalDatabus), .Q(PC2Data));  // open: carry
  Counter #(.max('hf), .width(4)) PC1 (
    .clr(HardwareReset), .load(and_24_out), .up(s_r_ff_2_qn), .count(1'b1), .clk(or_11_out), .D(Buffer1Data),
    .carry(PC1_carry), .Q(PC1Data));
  Counter #(.max('hf), .width(4)) PC0 (
    .clr(HardwareReset), .load(and_25_out), .up(s_r_ff_2_qn), .count(1'b1), .clk(or_12_out), .D(Buffer2Data),
    .carry(PC0_carry), .Q(PC0Data));
  Register #(.trigger("high"), .width(12)) AddressRegister (
    .D({PC2Data, PC1Data, PC0Data}), .en(or_13_out), .clk(or_13_out), .Q(ADDRESSBUS), .clr(HardwareReset));
  or or_13 (or_13_out, or_12_out, WriteToAddressRegister);

  // Other names for the same wires on the sheet: ZeroFlag = FlagsRegister[0];
  //   FlagsRegister[2:1] = {BorrowFlag, CarryFlag}; OddParityFlag = FlagsRegister[3];
  //   TestZeroFlag = TestFlagsRegister[0]; TestFlagsRegister[2:1] = {TestBorrowFlag, TestCarryFlag};
  //   TestOddParityFlag = TestFlagsRegister[3]

  // Notes on the sheet:
  //   contents of rom_1 (hex, n*v repeats v):
  //   0 b5 38 49 71 92*0 49 1 49 100 49 72 300*0 49
  //   Passive Flags
  //   Conditionals
  //   Active Flags
  //   Register Outputs to Databus
  //   Decoder
  //   Reset Handling
  //   Arithmetic Registers
  //   ALU
  //   Address Registers
endmodule
